# Fritzing sketch MainNode (saved by Fritzing 0.9.3b)

parts:
  Part1 = Arduino Mega 2560 (Rev3)
  Matrix_keypad1 = KEYPAD 4x4
  ZS-042_RTC1 = ZS-042 RTC Module
  YL-1 = YL-105 [part_number=YL-105]
  Part2 = NRF24L01+ Breakout Board  # not connected
  Part3 = Arduino GSM Shield
  Part4 = KY-012 Active Buzzer Module [package="Breakout board"]

nets:
  N1: Part1.D21/SCL, ZS-042_RTC1.SCL
  N2: Part1.D20/SDA, ZS-042_RTC1.SDA
  N3: Part1.D10_PWM, Part3.DSM_TX_D3
  N4: Part1.D9_PWM, Part4.I/0
  N5: Part1.D8_PWM, YL-1.CE
  N6: Part1.RESET, Part1.D4_PWM, Part3.RST_ARDUINO
  3V3: Part1.3V3, ZS-042_RTC1.VCC
  VCC: Part1.5V, YL-1.VCC, Part4.VCC
  GND: Part1.GND, ZS-042_RTC1.GND, YL-1.GND, Part3.AGND, Part4.GND
  VIN: Part1.VIN, Part3.VIN
  N7: Part1.D7_PWM, Part3.RST_MDM/D7
  N8: Part1.D22, Matrix_keypad1.col4
  N9: Part1.D23, Matrix_keypad1.row4
  N10: Part1.D24, Matrix_keypad1.col3
  N11: Part1.D25, Matrix_keypad1.row3
  N12: Part1.D26, Matrix_keypad1.col2
  N13: Part1.D27, Matrix_keypad1.row2
  N14: Part1.D28, Matrix_keypad1.col1
  N15: Part1.D29, Matrix_keypad1.row1
  N16: Part1.D50, YL-1.MISO
  N17: Part1.D51, YL-1.MOSI
  N18: Part1.D52, YL-1.SCK
  N19: Part1.D53, YL-1.CSN

custom parts:
  KEYPAD 4x4: Matrix keypad 16 buttons, 4 rows x 4 columns
  KY-012 Active Buzzer Module: Active Piezoelectric Buzzer Module Keyes KY-012, it produces single-tone sound when signal is high.
