# Fritzing sketch Node (saved by Fritzing 0.9.3b)
breadboards: 1

parts:
  Part1 = Arduino Nano (Rev3.0) (ICSP)
  part = 18650 battery holder [package=battery-18650-kit]
  part_2 = DC-DC 2-24V Step Up Booster [package=THT]
  YL-1 = YL-105 [part_number=YL-105]
  Part2 = NRF24L01+ Breakout Board  # not connected
  U2 = SWITCH_SPDT [package=kps-1290]

nets:
  GND: Part1.GND, part_2.pin1, YL-1.GND
  N1: Part1.D8, YL-1.CE
  N2: Part1.D10, YL-1.CSN
  N3: Part1.D11/MOSI, YL-1.MOSI
  N4: Part1.D12/MISO, YL-1.MISO
  VIN: Part1.VIN, part_2.pin2, YL-1.VCC
  N5: Part1.A0, part.+, part_2.pin3
  N6: Part1.D13/SCK, YL-1.SCK
  N7: part.-, U2.P
  N8: part_2.pin4, U2.O

custom parts:
  18650 battery holder: 18650 Battery Holder
  DC-DC 2-24V Step Up Booster: Convertisseur DC-DC 2-24V 2A
